# Fritzing sketch two_potentiometers (saved by Fritzing 0.9.2b)
breadboards: 1

parts:
  Part1 = Arduino Nano (Rev3.0)
  U1 = POT [package=pot_mammoth]
  U2 = POT [package=pot_mammoth]

nets:
  N1: Part1.GND, U1.E, U2.E
  N2: Part1.5V, U1.S, U2.S
  N3: Part1.A1, U2.A
  N4: Part1.A0, U1.A
