# Fritzing sketch rgb_led (saved by Fritzing 0.9.2b)
breadboards: 1

parts:
  Part1 = Arduino Nano (Rev3.0)
  R2 = Resistor [tolerance=±5% resistance=100 package=THT]
  R3 = Resistor [tolerance=±5% resistance=100 package=THT]
  LED1 = RGB LED (com. cathode, rbg) [package="5 mm [THT]"]
  R1 = Resistor [tolerance=±5% resistance=180 package=THT]

nets:
  N1: Part1.GND, LED1.red_anode
  N2: Part1.D9, R1.Pin_0
  N3: Part1.D10, R2.Pin_0
  N4: Part1.D11/MOSI, R3.Pin_0
  N5: R2.Pin_1, LED1.green_anode
  N6: R3.Pin_1, LED1.common_cathode
  N7: LED1.blue_anode, R1.Pin_1
