# Fritzing sketch rgb_switch (saved by Fritzing 0.9.2b)
breadboards: 1

parts:
  S1 = Pushbutton [package="[THT]"]
  S2 = Pushbutton [package="[THT]"]
  S3 = Pushbutton [package="[THT]"]
  Part1 = Arduino Nano (Rev3.0)
  R1 = Resistor [tolerance=±5% resistance=10k package=THT]
  R2 = Resistor [tolerance=±5% resistance=10k package=THT]
  R3 = Resistor [tolerance=±5% resistance=10k package=THT]

nets:
  N1: S1.Pin_1, S1.Pin_2, Part1.D5, R1.Pin_0
  N2: S1.Pin_3, S1.Pin_4, S2.Pin_3, S2.Pin_4, S3.Pin_3, S3.Pin_4, Part1.5V
  N3: S2.Pin_1, S2.Pin_2, Part1.D4, R2.Pin_0
  N4: S3.Pin_1, S3.Pin_2, Part1.D3, R3.Pin_0
  N5: Part1.GND, R1.Pin_1, R2.Pin_1, R3.Pin_1
